# Fritzing sketch BAKSAMPAH (saved by Fritzing 1.0.6)

parts:
  Capasitive = LJ18A3-B-Z/BY [package=THT]
  J1 = Basic Servo
  J2 = Basic Servo
  M2 = DOIT Esp32 DevKit v1 (30 pins long, 11 pins width) [part_number=ESP32S-PIN30]
  M3 = E18-D80NK_1 [package=THT]
  M4 = E18-D80NK_1 [package=THT]
  Capasitive_2 = LJ18A3-B-Z/BY [package=THT]
  Part1 = LCD1602-I2C
  DFRobot_DFPlayer_Mini1 = DFRobot DFPlayer Mini [part_number=DFR0299]
  SP1 = SPEAKER [package=pcb_mount_speaker]
  M5 = LJ18A3-B-Z/BY [package=THT]
  M6 = LJ18A3-B-Z/BY [package=THT]
  J3 = XL4015 DC-DC CC CV module (blue)
  U1 = RFID RC522 SIP - 8 pins [chip_label="RFID RC522" package="SIP (Single Inline) [THT]"]
  A1 = 2 channel relay module [package=THT]
  HC-SR04_Sensor_1 = HC-SR04 Ultrasonic Distance Sensor
  HC-SR04_Sensor_2 = HC-SR04 Ultrasonic Distance Sensor

nets:
  N1: Capasitive.SIG_(BLK), M2.D35
  GND: J1.gnd, J2.gnd, M2.GND, M3.pin1, M4.pin1, Part1.GND, DFRobot_DFPlayer_Mini1.GND-1, J3.pin_4, U1.GND, A1.pin_14
  VCC: J1.vcc, J2.vcc, M2.VIN, M3.pin2, M4.pin2, Capasitive_2.VI_(BRN), Part1.VCC, DFRobot_DFPlayer_Mini1.VCC, J3.pin_3, U1.VCC, A1.pin_13
  N2: J1.pulse, M2.D13
  N3: J2.pulse, M2.D12
  N4: M2.D15, HC-SR04_Sensor_2.ECHO
  N5: M2.D2, HC-SR04_Sensor_2.TRIG
  N6: M2.D4, U1.NSS
  N7: M2.RX2, DFRobot_DFPlayer_Mini1.TX
  N8: M2.TX2, DFRobot_DFPlayer_Mini1.RX
  N9: M2.D5, U1.RST
  N10: M2.D18, U1.SCK
  N11: M2.D19, U1.MISO
  N12: M2.D21, Part1.SDA
  N13: M2.D22, Part1.SCL
  N14: M2.D23, U1.MOSI
  N15: M2.VP, M3.pin3
  N16: M2.VN, M4.pin3
  N17: M2.D34, Capasitive_2.SIG_(BLK)
  N18: M2.D32, M5.SIG_(BLK)
  N19: M2.D33, M6.SIG_(BLK)
  N20: M2.D25, A1.pin_16
  N21: M2.D26, A1.pin_15
  N22: M2.D27, HC-SR04_Sensor_1.TRIG
  N23: M2.D14, HC-SR04_Sensor_1.ECHO
  N24: DFRobot_DFPlayer_Mini1.SPK_1, SP1.-
  N25: DFRobot_DFPlayer_Mini1.SPK_2, SP1.+
  N26: M5.VO_(BLU), M6.VO_(BLU)
  N27: M5.VI_(BRN), M6.VI_(BRN)

custom parts:
  LJ18A3-B-Z/BY: LJ18A3-B-Z/BX Proximity Sensor module.
  DOIT Esp32 DevKit v1 (30 pins long, 11 pins width): The DOIT Esp32 DevKit v1 is one of the development board created by DOIT to evaluate the ESP-WROOM-32 module. It is based on the ESP32 microcontroller that boasts Wifi, Bluetooth, Ethernet and Low Power support all in a single chip. (vanepp) made breadboard work, adjusted pin numbering and labels and reduced size of schematic and cleaned up pcb. This chip is 30pins long (2 x15) and 11 pins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
  E18-D80NK_1: E18-D80NK Proximity Sensor module.
  LCD1602-I2C: A standard character display, usually with 2x16 characters. Comes in many colors with LCM1602 IIC attached.
  XL4015 DC-DC CC CV module (blue): XL4015 DC-DC CC/CV module blue
  RFID RC522 SIP - 8 pins: A SIP stand-in part for RFID RC522 . With 8 pins on a 300 mil single inline package (SIP) footprint.
  2 channel relay module: 2 channel Relay Module 5V 12V 24V High and Low Level Trigger Relay Control With Optocoupler Two Way relays DC 5 V 12 V 24 V Volt.
